# Fritzing sketch wiring (saved by Fritzing 0.9.2b)
breadboards: 1

parts:
  U1 = NodeMCU V1.0
  Squix1 = OLED 0.96" 128x64 I2C SSD1306

nets:
  3V3: U1.3V3, Squix1.VCC
  GND: U1.GND, Squix1.GND
  N1: U1.D5, Squix1.SCA
  N2: U1.D6, Squix1.SCL

custom parts:
  NodeMCU V1.0: ESP9266 based NodeMCU
